# Fritzing sketch logic_level_shifter (saved by Fritzing 0.9.2b)
breadboards: 1

parts:
  Q1 = Basic FET N-Channel [package="TO220 [THT]"]
  Part1 = Arduino Uno (Rev3)
  R1 = Resistor [tolerance=±5% resistance=220 package=THT]
  R2 = Resistor [tolerance=±5% resistance=220 package=THT]

nets:
  N1: Q1.gate, Part1.3V3, R2.Pin_0
  N2: Q1.drain, R1.Pin_0
  N3: Q1.source, Part1.D13/SCK, R2.Pin_1
  N4: Part1.5V, R1.Pin_1
